# Fritzing sketch circuitoIR (saved by Fritzing 0.9.3b)
breadboards: 1

parts:
  Componente1 = Arduino Uno (Rev3)
  IR1 = TSOP312.., 314.. [package=THT]
  LED1 = LED - 5mm [color="Green (565nm)" package="5 mm [THT]"]
  R1 = Resistor [tolerance=±5% resistance=220 package=THT]
  R2 = Resistor [tolerance=±5% resistance=20 package=THT]  # not connected

nets:
  N1: Componente1.D2, IR1.Data
  N2: Componente1.D5_PWM, LED1.cathode
  GND: Componente1.GND, IR1.GND, R1.Pin_1
  N3: LED1.anode, R1.Pin_0
