# Fritzing sketch circuito_3_way_rele (saved by Fritzing 0.9.3b)

parts:
  Fonte = 4 x AAA Battery Mount
  Componente1 = Módulo Relé
  Componente2 = Módulo Relé
  S1 = SWITCH-MOMENTARY-2 [package=tactile-switch-1101ne]
  Componente3 = Arduino Nano (Rev3.0)
  Fonte1 = 4 x AAA Battery Mount
  LED2 = LED - 5mm [color="Red (633nm)" package="5 mm [THT]"]
  S2 = SWITCH-MOMENTARY-2 [package=tactile-switch-1101ne]
  Coelba = 4 x AAA Battery Mount
  Componente4 = ACS712 Low Current Sensor Board v12
  LED1 = LED - 5mm [color="Red (633nm)" package="5 mm [THT]"]

nets:
  N1: Fonte.-, Componente1.GND
  N2: Fonte.+, Componente1.5V, S1.1
  N3: Componente1.In, S1.2
  N4: Componente1.NA, Componente2.NF
  N5: Componente1.C, Coelba.-
  N6: Componente1.NF, Componente2.NA
  N7: Componente2.In, Componente3.D10
  5V: Componente2.5V, Componente3.5V, Componente4.5V
  GND: Componente2.GND, Componente3.GND, Componente4.GND
  N8: Componente2.C, LED1.cathode
  N9: Componente3.D9, Componente4.VO
  N10: Fonte1.-, LED2.cathode
  N11: Fonte1.+, S2.1
  N12: LED2.anode, S2.2
  N13: Coelba.+, Componente4.IP+
  N14: Componente4.IP-, LED1.anode

custom parts:
  Módulo Relé: Este modulo pode ser usado em diversos projetos afim de acionar cargas de até 250VAC @ 7A ou 125VAC @ 10A. Pode ser usado para controlar luzes, equipamentos ligados a rede elétrica, motores, etc. Você pode fazer uma ponte-H baseada em relés com alguns destes módulos.
