# Fritzing sketch circuitov1 (saved by Fritzing 0.9.3b)

parts:
  Componente1 = Arduino Uno (Rev3)
  Raspberry_Pi2_Modelo_B = Raspberry Pi 2
  Interruptor = Toggle Switch [package=THT]
  Lâmpada = LEDs [package=led10mm]
  VCC2 = Battery block 9V
  Interruptor_2 = Toggle Switch [package=THT]
  Interruptor_3 = Toggle Switch [package=THT]
  Lâmpada_2 = LEDs [package=led10mm]
  Lâmpada_3 = LEDs [package=led10mm]
  Sensor_de_Corrente = ACS712 Low Current Sensor Board v12
  VCC3 = Battery block 9V
  Sensor_PIR = LM34 [package=so08]
  Relé = Módulo Relé
  Emissor_Infra_red = Max Power IR LED Kit
  Sensor_de_Corrente1 = ACS712 Low Current Sensor Board v12
  Sensor_de_Corrente2 = ACS712 Low Current Sensor Board v12

nets:
  N1: Componente1.D8, Sensor_de_Corrente.VO
  N2: Componente1.D0/RX, Raspberry_Pi2_Modelo_B.GPIO14
  N3: Componente1.D1/TX, Raspberry_Pi2_Modelo_B.GPIO15
  N4: Componente1.D2, Emissor_Infra_red.CONTROL
  N5: Componente1.D3_PWM, Sensor_PIR.VOUT
  N6: Componente1.D4, Relé.In
  N7: Componente1.D6_PWM, Sensor_de_Corrente2.VO
  N8: Componente1.D7, Sensor_de_Corrente1.VO
  N9: Interruptor.COM, Lâmpada_2.C
  N10: Interruptor.L2, VCC2.-, Interruptor_2.L2, Interruptor_3.L2, Sensor_de_Corrente.IP-, Sensor_de_Corrente1.IP-, Sensor_de_Corrente2.IP-
  N11: Lâmpada.C, Interruptor_3.COM, Relé.NA
  N12: Lâmpada.A, VCC2.+, Lâmpada_2.A, Lâmpada_3.A, Sensor_de_Corrente.IP+, Relé.C, Sensor_de_Corrente1.IP+, Sensor_de_Corrente2.IP+
  N13: Interruptor_2.COM, Lâmpada_3.C
  5V: Sensor_de_Corrente.5V, VCC3.+, Sensor_PIR.V+, Relé.5V, Emissor_Infra_red.VCC, Sensor_de_Corrente1.5V, Sensor_de_Corrente2.5V
  GND: Sensor_de_Corrente.GND, Emissor_Infra_red.GND, Sensor_de_Corrente1.GND, Sensor_de_Corrente2.GND
  GND_2: VCC3.-, Sensor_PIR.GND, Relé.GND

custom parts:
  Módulo Relé: Este modulo pode ser usado em diversos projetos afim de acionar cargas de até 250VAC @ 7A ou 125VAC @ 10A. Pode ser usado para controlar luzes, equipamentos ligados a rede elétrica, motores, etc. Você pode fazer uma ponte-H baseada em relés com alguns destes módulos.
