# Fritzing sketch circuitov3 (saved by Fritzing 0.9.3b)

parts:
  Componente1 = Arduino Uno (Rev3)
  Interruptor = Toggle Switch [package=THT]
  Lâmpada = LEDs [package=led10mm]
  VCC2 = Battery block 9V
  Interruptor_2 = Toggle Switch [package=THT]
  Interruptor_3 = Toggle Switch [package=THT]
  Lâmpada_2 = LEDs [package=led10mm]
  Lâmpada_3 = LEDs [package=led10mm]
  Sensor_de_Corrente = ACS712 Low Current Sensor Board v12
  VCC3 = Battery block 9V
  Sensor_PIR = LM34 [package=so08]
  Relé = Módulo Relé
  Emissor_Infra_red = Max Power IR LED Kit
  Sensor_de_Corrente1 = ACS712 Low Current Sensor Board v12
  Sensor_de_Corrente2 = ACS712 Low Current Sensor Board v12
  Sensor_PIR1 = LM34 [package=so08]
  Transceiver_ABC = NRF24L01+ Breakout Board
  Transceiver_A = NRF24L01+ Breakout Board
  Raspberry_Pi2_Modelo_B = Raspberry Pi 2

nets:
  N1: Componente1.D8, Sensor_PIR1.VOUT
  N2: Componente1.D9_PWM, Sensor_PIR.VOUT
  N3: Componente1.D10_PWM/SS, Sensor_de_Corrente2.VO
  N4: Componente1.D11_PWM/MOSI, Sensor_de_Corrente1.VO
  N5: Componente1.D12/MISO, Sensor_de_Corrente.VO
  N6: Componente1.D13/SCK, Relé.In
  GND: Componente1.GND, Transceiver_A.GND
  N7: Componente1.D2, Transceiver_A.CE
  N8: Componente1.D3_PWM, Transceiver_A.SCK
  N9: Componente1.D4, Transceiver_A.MISO
  N10: Componente1.D5_PWM, Transceiver_A.MOSI
  N11: Componente1.D6_PWM, Transceiver_A.CS
  N12: Componente1.D7, Emissor_Infra_red.CONTROL
  3V3: Componente1.3V3, Transceiver_A.VCC
  N13: Interruptor.COM, Lâmpada.C, Interruptor_2.COM, Interruptor_3.COM, Lâmpada_2.C, Lâmpada_3.C, Relé.NA
  N14: Interruptor.L2, VCC2.-, Interruptor_2.L2, Interruptor_3.L2, Sensor_de_Corrente.IP-, Sensor_de_Corrente1.IP-, Sensor_de_Corrente2.IP-
  N15: Lâmpada.A, VCC2.+, Lâmpada_2.A, Lâmpada_3.A, Sensor_de_Corrente.IP+, Relé.C, Sensor_de_Corrente1.IP+, Sensor_de_Corrente2.IP+
  5V: Sensor_de_Corrente.5V, VCC3.+, Sensor_PIR.V+, Relé.5V, Emissor_Infra_red.VCC, Sensor_de_Corrente1.5V, Sensor_de_Corrente2.5V, Sensor_PIR1.V+
  GND_2: Sensor_de_Corrente.GND, VCC3.-, Sensor_PIR.GND, Emissor_Infra_red.GND, Sensor_de_Corrente1.GND, Sensor_de_Corrente2.GND, Sensor_PIR1.GND
  GND_3: Transceiver_ABC.GND, Raspberry_Pi2_Modelo_B.GND
  VCC: Transceiver_ABC.VCC, Raspberry_Pi2_Modelo_B.3v3
  N16: Transceiver_ABC.CE, Raspberry_Pi2_Modelo_B.GPIO16
  N17: Transceiver_ABC.CS, Raspberry_Pi2_Modelo_B.GPIO20
  N18: Transceiver_ABC.SCK, Raspberry_Pi2_Modelo_B.GPIO26
  N19: Transceiver_ABC.MOSI, Raspberry_Pi2_Modelo_B.GPIO19
  N20: Transceiver_ABC.MISO, Raspberry_Pi2_Modelo_B.GPIO13

custom parts:
  Módulo Relé: Este modulo pode ser usado em diversos projetos afim de acionar cargas de até 250VAC @ 7A ou 125VAC @ 10A. Pode ser usado para controlar luzes, equipamentos ligados a rede elétrica, motores, etc. Você pode fazer uma ponte-H baseada em relés com alguns destes módulos.
