# Fritzing sketch circuitov4 (saved by Fritzing 0.9.3b)

parts:
  Componente1 = Arduino Uno (Rev3)
  Lâmpada = LEDs [package=led10mm]
  VCC2 = Battery block 9V
  Sensor_de_Corrente = ACS712 Low Current Sensor Board v12
  VCC3 = Battery block 9V
  Sensor_PIR = LM34 [package=so08]
  Emissor_Infra_red = Max Power IR LED Kit
  Sensor_PIR1 = LM34 [package=so08]
  Transceiver_ABC = NRF24L01+ Breakout Board
  Transceiver_A = NRF24L01+ Breakout Board
  Raspberry_Pi2_Modelo_B = Raspberry Pi 2
  S1 = Pushbutton [package=THT]
  Componente3 = Módulo Relé
  Componente4 = Módulo Relé
  VCC4 = Battery block 9V
  S2 = Pushbutton [package=THT]
  Componente5 = Módulo Relé
  Componente6 = Módulo Relé
  VCC5 = Battery block 9V
  Lâmpada1 = LEDs [package=led10mm]
  Sensor_de_Corrente1 = ACS712 Low Current Sensor Board v12
  S3 = Pushbutton [package=THT]
  Componente7 = Módulo Relé
  Componente8 = Módulo Relé
  VCC7 = Battery block 9V
  Lâmpada2 = LEDs [package=led10mm]
  Sensor_de_Corrente2 = ACS712 Low Current Sensor Board v12

nets:
  N1: Componente1.D8, Sensor_PIR1.VOUT
  N2: Componente1.D9_PWM, Sensor_PIR.VOUT
  N3: Componente1.D10_PWM/SS, Sensor_de_Corrente2.VO
  N4: Componente1.D11_PWM/MOSI, Sensor_de_Corrente1.VO
  N5: Componente1.D12/MISO, Sensor_de_Corrente.VO
  N6: Componente1.D13/SCK, Componente8.In
  GND: Componente1.GND, Transceiver_A.GND
  N7: Componente1.AREF, Componente4.In
  N8: Componente1.D2, Transceiver_A.CE
  N9: Componente1.D3_PWM, Transceiver_A.SCK
  N10: Componente1.D4, Transceiver_A.MISO
  N11: Componente1.D5_PWM, Transceiver_A.MOSI
  N12: Componente1.D6_PWM, Transceiver_A.CS
  N13: Componente1.D7, Emissor_Infra_red.CONTROL
  N14: Componente1.RESET, Componente6.In
  3V3: Componente1.3V3, Transceiver_A.VCC
  N15: Lâmpada.C, Componente4.C
  N16: Lâmpada.A, Sensor_de_Corrente.IP-
  N17: VCC2.-, Componente3.GND
  N18: VCC2.+, S1.leg1, Componente3.5V
  5V: Sensor_de_Corrente.5V, VCC3.+, Sensor_PIR.V+, Emissor_Infra_red.VCC, Sensor_PIR1.V+, Componente4.5V, Componente6.5V, Sensor_de_Corrente1.5V, Componente8.5V, Sensor_de_Corrente2.5V
  GND_2: Sensor_de_Corrente.GND, VCC3.-, Sensor_PIR.GND, Emissor_Infra_red.GND, Sensor_PIR1.GND, Sensor_de_Corrente1.GND, Sensor_de_Corrente2.GND
  N19: Sensor_de_Corrente.IP+, VCC4.-, Sensor_de_Corrente1.IP+, Sensor_de_Corrente2.IP+
  GND_3: Transceiver_ABC.GND, Raspberry_Pi2_Modelo_B.GND
  VCC: Transceiver_ABC.VCC, Raspberry_Pi2_Modelo_B.3v3
  N20: Transceiver_ABC.CE, Raspberry_Pi2_Modelo_B.GPIO16
  N21: Transceiver_ABC.CS, Raspberry_Pi2_Modelo_B.GPIO20
  N22: Transceiver_ABC.SCK, Raspberry_Pi2_Modelo_B.GPIO26
  N23: Transceiver_ABC.MOSI, Raspberry_Pi2_Modelo_B.GPIO19
  N24: Transceiver_ABC.MISO, Raspberry_Pi2_Modelo_B.GPIO13
  N25: S1.leg0, Componente3.In
  N26: Componente3.NA, Componente4.NF
  N27: Componente3.C, VCC4.+, Componente5.C, Componente7.C
  N28: Componente3.NF, Componente4.NA
  N29: S2.leg0, Componente5.In
  N30: S2.leg1, Componente5.5V, VCC5.+
  N31: Componente5.GND, VCC5.-
  N32: Componente5.NA, Componente6.NF
  N33: Componente5.NF, Componente6.NA
  N34: Componente6.C, Lâmpada1.C
  N35: Lâmpada1.A, Sensor_de_Corrente1.IP-
  N36: S3.leg0, Componente7.In
  N37: S3.leg1, Componente7.5V, VCC7.+
  N38: Componente7.GND, VCC7.-
  N39: Componente7.NA, Componente8.NF
  N40: Componente7.NF, Componente8.NA
  N41: Componente8.C, Lâmpada2.C
  N42: Lâmpada2.A, Sensor_de_Corrente2.IP-

custom parts:
  Módulo Relé: Este modulo pode ser usado em diversos projetos afim de acionar cargas de até 250VAC @ 7A ou 125VAC @ 10A. Pode ser usado para controlar luzes, equipamentos ligados a rede elétrica, motores, etc. Você pode fazer uma ponte-H baseada em relés com alguns destes módulos.
