# Fritzing sketch circuitov5 (saved by Fritzing 0.9.3b)

parts:
  Componente1 = Arduino Uno (Rev3)
  Lâmpada = LEDs [package=led10mm]
  Sensor_de_Corrente = ACS712 Low Current Sensor Board v12
  VCC3 = Battery block 9V
  Sensor_PIR = LM34 [package=so08]
  Emissor_Infra_red = Max Power IR LED Kit
  Sensor_PIR1 = LM34 [package=so08]
  Transceiver_ABC = NRF24L01+ Breakout Board
  Transceiver_A = NRF24L01+ Breakout Board
  Raspberry_Pi2_Modelo_B = Raspberry Pi 2
  S1 = Pushbutton [package=THT]
  Componente3 = Módulo Relé
  Componente4 = Módulo Relé
  220V = Battery block 9V
  S2 = Pushbutton [package=THT]
  Componente5 = Módulo Relé
  Componente6 = Módulo Relé
  VCC4 = Battery block 9V
  Lâmpada1 = LEDs [package=led10mm]
  Sensor_de_Corrente1 = ACS712 Low Current Sensor Board v12
  S3 = Pushbutton [package=THT]
  Componente7 = Módulo Relé
  Componente8 = Módulo Relé
  Lâmpada2 = LEDs [package=led10mm]
  Sensor_de_Corrente2 = ACS712 Low Current Sensor Board v12
  VCC5 = Battery block 9V

nets:
  N1: Componente1.D8, Componente4.In
  N2: Componente1.D9_PWM, Transceiver_A.CE
  N3: Componente1.D10_PWM/SS, Transceiver_A.CS
  N4: Componente1.D11_PWM/MOSI, Transceiver_A.MOSI
  N5: Componente1.D12/MISO, Transceiver_A.MISO
  N6: Componente1.D13/SCK, Transceiver_A.SCK
  GND: Componente1.GND, Transceiver_A.GND
  N7: Componente1.D0/RX, Emissor_Infra_red.CONTROL
  N8: Componente1.D1/TX, Sensor_PIR1.VOUT
  N9: Componente1.D2, Sensor_PIR.VOUT
  N10: Componente1.D3_PWM, Sensor_de_Corrente.VO
  N11: Componente1.D4, Sensor_de_Corrente1.VO
  N12: Componente1.D5_PWM, Sensor_de_Corrente2.VO
  N13: Componente1.D6_PWM, Componente8.In
  N14: Componente1.D7, Componente6.In
  3V3: Componente1.3V3, Transceiver_A.VCC
  N15: Lâmpada.C, Sensor_de_Corrente.IP-
  N16: Lâmpada.A, 220V.-, Lâmpada1.A, Lâmpada2.A
  N17: Sensor_de_Corrente.IP+, Componente3.C
  5V: Sensor_de_Corrente.5V, S1.leg1, Componente3.5V, S2.leg1, Componente5.5V, VCC4.+, Sensor_de_Corrente1.5V, S3.leg1, Componente7.5V, Sensor_de_Corrente2.5V
  GND_2: Sensor_de_Corrente.GND, Componente3.GND, Componente5.GND, VCC4.-, Sensor_de_Corrente1.GND, Componente7.GND, Sensor_de_Corrente2.GND
  GND_3: VCC3.-, Sensor_PIR.GND, Emissor_Infra_red.GND, Sensor_PIR1.GND
  N18: VCC3.+, Sensor_PIR.V+, Emissor_Infra_red.VCC, Sensor_PIR1.V+
  GND_4: Transceiver_ABC.GND, Raspberry_Pi2_Modelo_B.GND
  VCC: Transceiver_ABC.VCC, Raspberry_Pi2_Modelo_B.3v3
  N19: Transceiver_ABC.CE, Raspberry_Pi2_Modelo_B.GPIO16
  N20: Transceiver_ABC.CS, Raspberry_Pi2_Modelo_B.GPIO20
  N21: Transceiver_ABC.SCK, Raspberry_Pi2_Modelo_B.GPIO26
  N22: Transceiver_ABC.MOSI, Raspberry_Pi2_Modelo_B.GPIO19
  N23: Transceiver_ABC.MISO, Raspberry_Pi2_Modelo_B.GPIO13
  N24: S1.leg0, Componente3.In
  N25: Componente3.NA, Componente4.NF
  N26: Componente3.NF, Componente4.NA
  5V_2: Componente4.5V, Componente6.5V, Componente8.5V, VCC5.+
  GND_5: Componente4.GND, Componente6.GND, Componente8.GND, VCC5.-
  N27: Componente4.C, 220V.+, Componente6.C, Componente8.C
  N28: S2.leg0, Componente5.In
  N29: Componente5.NA, Componente6.NF
  N30: Componente5.C, Sensor_de_Corrente1.IP+
  N31: Componente5.NF, Componente6.NA
  N32: Lâmpada1.C, Sensor_de_Corrente1.IP-
  N33: S3.leg0, Componente7.In
  N34: Componente7.NA, Componente8.NF
  N35: Componente7.C, Sensor_de_Corrente2.IP+
  N36: Componente7.NF, Componente8.NA
  N37: Lâmpada2.C, Sensor_de_Corrente2.IP-

custom parts:
  Módulo Relé: Este modulo pode ser usado em diversos projetos afim de acionar cargas de até 250VAC @ 7A ou 125VAC @ 10A. Pode ser usado para controlar luzes, equipamentos ligados a rede elétrica, motores, etc. Você pode fazer uma ponte-H baseada em relés com alguns destes módulos.
